// Logisim project ISA.circ as structural Verilog: 3 circuits, main circuit Main
module Main (
);

  wire clock_1_out;
  wire [7:0] UC_data;
  wire [31:0] b_reg_1_saida_1, b_reg_1_saida_2, multiplexer_1_out, ula_1_saida;

  Clock clock_1 (.out(clock_1_out));
  Register PC (.clk(clock_1_out));  // open: D, en, Q, clr
  ROM #(.addrWidth(24), .dataWidth(24)) rom_1 ();  // open: addr, data
  B_REG b_reg_1 (.CLK(clock_1_out), .SAIDA_1(b_reg_1_saida_1), .SAIDA_2(b_reg_1_saida_2));  // open: DATA, RD, RS1, RS2
  Multiplexer #(.width(32)) multiplexer_1 (.in0(b_reg_1_saida_2), .out(multiplexer_1_out));  // open: in1, sel
  ULA ula_1 (.rs1(b_reg_1_saida_1), .rs2(multiplexer_1_out), .SAIDA(ula_1_saida));  // open: ULA_CONTROL
  ROM UC (.data(UC_data));  // open: addr
  RAM #(.addrWidth(24), .dataWidth(32)) M_DADOS (
    .addr(ula_1_saida[23:0]), .we(UC_data[0]), .oe(1'b1), .clk(clock_1_out), .din(b_reg_1_saida_2));  // open: dout
  // Pins of 1 and 8 bits meet at UC_data

  // Notes on the sheet:
  //   contents of rom_1 (hex, n*v repeats v):
  //   443 8443 10443 18443 20443 28443 30443 38443 808800 908800 a08800 b08800 c08800 d08800 e08800 f08800
  //   10e0 2010e0 4010e0 6010e0 8010e0 840000 608800
endmodule

module ULA (
  input  [31:0] rs1,
  input  [31:0] rs2,
  input  [2:0] ULA_CONTROL,
  output [31:0] SAIDA
);

  wire comparator_1_eq;
  wire [31:0] adder_1_out, and_1_out, multiplexer_1_out, not_1_out, or_1_out, shifter_1_out, shifter_2_out,
       subtractor_1_out, xor_1_out;

  Comparator #(.width(27)) comparator_1 (.a({27{1'b0}}), .b(rs2[31:5]), .eq(comparator_1_eq));  // open: gt, lt
  Multiplexer #(.width(32)) multiplexer_1 (.in0({32{1'b0}}), .in1(rs1), .out(multiplexer_1_out), .sel(comparator_1_eq));
  Adder #(.width(32)) adder_1 (.a(rs1), .b(rs2), .out(adder_1_out));  // open: cin, cout
  Subtractor #(.width(32)) subtractor_1 (.a(rs1), .b(rs2), .out(subtractor_1_out));  // open: bin, bout
  Shifter #(.width(32)) shifter_1 (.in(multiplexer_1_out), .\dist (rs2[4:0]), .out(shifter_1_out));
  Shifter #(.shift("lr"), .width(32)) shifter_2 (.in(multiplexer_1_out), .\dist (rs2[4:0]), .out(shifter_2_out));
  assign and_1_out = rs1 & rs2;  // AND_Gate and_1, 32 bits wide
  assign or_1_out = rs1 | rs2;  // OR_Gate or_1, 32 bits wide
  assign xor_1_out = rs1 ^ rs2;  // XOR_Gate xor_1, 32 bits wide
  assign not_1_out = ~rs1;  // NOT_Gate not_1, 32 bits wide
  Multiplexer #(.select(3), .width(32)) multiplexer_2 (
    .in0(adder_1_out), .in1(subtractor_1_out), .in2(shifter_1_out), .in3(shifter_2_out), .in4(and_1_out),
    .in5(or_1_out), .in6(xor_1_out), .in7(not_1_out), .out(SAIDA), .sel(ULA_CONTROL));

  // Notes on the sheet:
  //   shift control
endmodule

module B_REG (
  input  [31:0] DATA,
  input  CLK,
  input  [2:0] RD,
  input  [2:0] RS1,
  input  [2:0] RS2,
  output [31:0] SAIDA_1,
  output [31:0] SAIDA_2
);

  wire demultiplexer_1_out0, demultiplexer_1_out1, demultiplexer_1_out2, demultiplexer_1_out3,
       demultiplexer_1_out4, demultiplexer_1_out5, demultiplexer_1_out6, demultiplexer_1_out7;
  wire [31:0] R0, R1, R2, R3, R4, R5, R6, R7;

  Demultiplexer #(.select(3)) demultiplexer_1 (
    .out0(demultiplexer_1_out0), .out1(demultiplexer_1_out1), .out2(demultiplexer_1_out2),
    .out3(demultiplexer_1_out3), .out4(demultiplexer_1_out4), .out5(demultiplexer_1_out5),
    .out6(demultiplexer_1_out6), .out7(demultiplexer_1_out7), .in(CLK), .sel(RD));
  Register #(.width(32)) register_1 (.D(DATA), .en(demultiplexer_1_out0), .Q(R0));  // open: clk, clr
  Register #(.width(32)) register_2 (.D(DATA), .en(demultiplexer_1_out1), .Q(R1));  // open: clk, clr
  Register #(.width(32)) register_3 (.D(DATA), .en(demultiplexer_1_out2), .Q(R2));  // open: clk, clr
  Register #(.width(32)) register_4 (.D(DATA), .en(demultiplexer_1_out3), .Q(R3));  // open: clk, clr
  Register #(.width(32)) register_5 (.D(DATA), .en(demultiplexer_1_out4), .Q(R4));  // open: clk, clr
  Register #(.width(32)) register_6 (.D(DATA), .en(demultiplexer_1_out5), .Q(R5));  // open: clk, clr
  Register #(.width(32)) register_7 (.D(DATA), .en(demultiplexer_1_out6), .Q(R6));  // open: clk, clr
  Register #(.width(32)) register_8 (.D(DATA), .en(demultiplexer_1_out7), .Q(R7));  // open: clk, clr
  Multiplexer #(.select(3), .width(32)) multiplexer_1 (
    .in0(R0), .in1(R1), .in2(R2), .in3(R3), .in4(R4), .in5(R5), .in6(R6), .in7(R7), .out(SAIDA_1), .sel(RS1));
  Multiplexer #(.select(3), .width(32)) multiplexer_2 (
    .in0(R0), .in1(R1), .in2(R2), .in3(R3), .in4(R4), .in5(R5), .in6(R6), .in7(R7), .out(SAIDA_2), .sel(RS2));
endmodule
